# Fritzing sketch ESP32-cam prog (saved by Fritzing 0.9.3b)

parts:
  Mod1 = ESP32 - CAM
  Súčiastka1 = FTDI Basic Programmer

nets:
  N1: Mod1.5V, Súčiastka1.POWER
  GND: Mod1.GND, Mod1.IO0, Súčiastka1.GND
  N2: Mod1.VOT, Súčiastka1.RXI
  N3: Mod1.VOR, Súčiastka1.TXO

notes:
  GND
  VCC +5V
  RX
  TX
  U0R
  U0T
  IO0
  +5V

custom parts:
  ESP32 - CAM: The ESP32-CAM has a very competitive small-size camera module that can operate independently as a minimum system with a footprint of only 27*40.5*4.5mm and a deep sleep current of up to 6mA.
  FTDI Basic Programmer: Description: This is the newest revision of our FTDI Basic. We now use a SMD 6-pin header on the bottom, which makes it smaller and more compact. Functionality has remained the same. This is a basic breakout board for the FTDI FT232RL USB to serial IC. The pinout of this board matches the FTDI cable to work with official Arduino and cloned 3.3V Arduino boards. It can also be used for general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
