# Fritzing sketch relay_flash (saved by Fritzing 0.9.3b)

parts:
  Mod1 = ESP32 - CAM
  JACK1 = 2.1mm Barrel Jack with Terminal Block
  KF-1 = KF-301 Relay [package=THT]
  A1 = RGB Strip LED

nets:
  N1: Mod1.5V, KF-1.power
  N2: Mod1.GND, KF-1.ground
  N3: Mod1.IO13, KF-1.signal
  N4: JACK1.POS, KF-1.NO
  N5: JACK1.NEG, A1.Blue_Connect
  N6: KF-1.C, A1.Common_Connect

custom parts:
  ESP32 - CAM: The ESP32-CAM has a very competitive small-size camera module that can operate independently as a minimum system with a footprint of only 27*40.5*4.5mm and a deep sleep current of up to 6mA.
  KF-301 Relay: KF-301
  RGB Strip LED: A tri-color Strip LED with red, green and blue. Pin order: red - common cathode - blue - green
