# Fritzing sketch dht22 (saved by Fritzing 0.9.3b)

parts:
  A1 = ESP32 wrover cam
  A2 = DHT22 module

nets:
  N1: A1.Pin_1, A2.VCC
  N2: A1.Pin_14, A2.GND
  N3: A1.Pin_15, A2.DAT

custom parts:
  ESP32 wrover cam: ESP32-WROVER -> A powerful and small controller with onboard camera and wireless.
  DHT22 module: DHT22 module. Pins GND VCC Data.
