# Fritzing sketch led_sch (saved by Fritzing 0.9.3b)

parts:
  A1 = ESP32 wrover cam
  KF-1 = KF-301 Relay [package=THT]
  JACK1 = 2.1mm Barrel Jack with Terminal Block
  A2 = RGB Strip LED

nets:
  N1: A1.Pin_12, KF-1.signal
  N2: A1.Pin_14, A1.Pin_40, KF-1.ground
  N3: A1.Pin_19, A1.Pin_20, KF-1.power
  N4: KF-1.C, JACK1.POS
  N5: KF-1.NO, A2.Common_Connect
  N6: JACK1.NEG, A2.Blue_Connect

custom parts:
  ESP32 wrover cam: ESP32-WROVER -> A powerful and small controller with onboard camera and wireless.
  KF-301 Relay: KF-301
  RGB Strip LED: A tri-color Strip LED with red, green and blue. Pin order: red - common cathode - blue - green
