# Fritzing sketch dht22 (saved by Fritzing 0.9.3b)

parts:
  ESP32S1 = XIAO ESP32S3(SENCE) [chip_label=ESP32S3(sense)]
  A1 = DHT22 module

nets:
  N1: ESP32S1.D0, A1.DAT
  3V3: ESP32S1.3V3, A1.VCC
  GND: ESP32S1.GND, A1.GND

custom parts:
  XIAO ESP32S3(SENCE): Seeed Studio XIAO ESP32S3 leverages dual-core ESP32S3 chip, supporting both Wi-Fi and BLE wireless connectivities, which allows battery charge. It integrates built-in camera sensor, digital microphone. It offers 8MB PSRAM, 8MB FLASH, and external SD card slot. All of these make it suitable for embedded ML, like intelligent voice and vision AI.
  DHT22 module: DHT22 module. Pins GND VCC Data.
