# Fritzing sketch led strip (saved by Fritzing 0.9.3b)

parts:
  ESP32S1 = XIAO ESP32S3(SENCE) [chip_label=ESP32S3(sense)]
  KF-1 = KF-301 Relay [package=THT]
  A1 = RGB Strip LED
  JACK1 = 2.1mm Barrel Jack with Terminal Block

nets:
  N1: ESP32S1.D3, KF-1.signal
  N2: ESP32S1.GND, KF-1.ground
  N3: ESP32S1.5V, KF-1.power
  N4: KF-1.C, A1.Common_Connect
  N5: KF-1.NO, JACK1.POS
  N6: A1.Blue_Connect, JACK1.NEG

custom parts:
  XIAO ESP32S3(SENCE): Seeed Studio XIAO ESP32S3 leverages dual-core ESP32S3 chip, supporting both Wi-Fi and BLE wireless connectivities, which allows battery charge. It integrates built-in camera sensor, digital microphone. It offers 8MB PSRAM, 8MB FLASH, and external SD card slot. All of these make it suitable for embedded ML, like intelligent voice and vision AI.
  KF-301 Relay: KF-301
  RGB Strip LED: A tri-color Strip LED with red, green and blue. Pin order: red - common cathode - blue - green
